// Logisim project ejercici 26 de febrero simpl.circ as structural Verilog
module alarma (
  input  A,
  input  B,
  input  C,
  output Y
);

  wire and_1_out;

  and and_1 (and_1_out, B, C);
  or or_1 (Y, and_1_out, A);
endmodule
