// Logisim project ejercicio 12 de marzo 2.circ as structural Verilog: 1 circuit, main circuit main
module main (
  input  in_1,
  input  PRESET,
  input  CLEAR,
  output A,
  output B,
  output C,
  output D
);

  wire button_1_out;

  Button button_1 (.out(button_1_out));
  J_K_Flip_Flop j_k_ff_1 (
    .J(in_1), .clk(button_1_out), .K(in_1), .Q(A), .preset(PRESET), .reset(CLEAR));  // open: Qn, en
  J_K_Flip_Flop j_k_ff_2 (.J(in_1), .clk(A), .K(in_1), .Q(B), .preset(PRESET), .reset(CLEAR));  // open: Qn, en
  J_K_Flip_Flop j_k_ff_3 (.J(in_1), .clk(B), .K(in_1), .Q(C), .preset(PRESET), .reset(CLEAR));  // open: Qn, en
  J_K_Flip_Flop j_k_ff_4 (.J(in_1), .clk(C), .K(in_1), .Q(D), .preset(PRESET), .reset(CLEAR));  // open: Qn, en
endmodule
