// Logisim project ejercicio 12 de marzo 3.circ as structural Verilog: 1 circuit, main circuit main
module main (
  input  in_1,
  input  PRESET,
  input  CLEAR,
  output A___8,
  output B___4,
  output C___2,
  output D___1,
  output out_8
);

  wire not_1_out, not_2_out, not_3_out, not_4_out;

  Button CLK (.out(out_8));
  not not_1 (not_1_out, out_8);
  J_K_Flip_Flop j_k_ff_1 (
    .J(in_1), .clk(not_1_out), .K(in_1), .Q(D___1), .preset(PRESET), .reset(CLEAR));  // open: Qn, en
  not not_2 (not_2_out, D___1);
  J_K_Flip_Flop j_k_ff_2 (
    .J(in_1), .clk(not_2_out), .K(in_1), .Q(C___2), .preset(PRESET), .reset(CLEAR));  // open: Qn, en
  not not_3 (not_3_out, C___2);
  J_K_Flip_Flop j_k_ff_3 (
    .J(in_1), .clk(not_3_out), .K(in_1), .Q(B___4), .preset(PRESET), .reset(CLEAR));  // open: Qn, en
  not not_4 (not_4_out, B___4);
  J_K_Flip_Flop j_k_ff_4 (
    .J(in_1), .clk(not_4_out), .K(in_1), .Q(A___8), .preset(PRESET), .reset(CLEAR));  // open: Qn, en
endmodule
