// Logisim project ejercicio 19 de marzo display 7 segmentos.circ as structural Verilog: 1 circuit, main circuit Display 7 segmentos
module Display_7_segmentos (
  input  in_1,
  input  PRESET,
  input  CLEAR
);

  wire and_1_out, and_2_out, and_3_out, and_4_out, and_5_out, and_6_out, and_7_out, and_8_out, and_9_out,
       and_10_out, and_11_out, and_12_out, and_13_out, and_14_out, and_15_out, and_16_out, CLK_out,
       j_k_ff_1_q, j_k_ff_2_q, j_k_ff_3_q, j_k_ff_4_q, not_1_out, not_2_out, not_3_out, not_4_out, not_5_out,
       not_6_out, not_7_out, not_8_out, not_9_out, not_10_out, not_11_out, not_12_out, not_13_out,
       not_14_out, not_15_out, not_16_out, not_17_out, not_18_out, not_19_out, not_20_out, not_21_out,
       not_22_out, not_23_out, not_24_out, or_1_out, or_2_out, or_3_out, or_4_out, or_5_out, or_6_out,
       or_7_out;

  Button CLK (.out(CLK_out));
  not not_1 (not_1_out, j_k_ff_1_q);
  not not_2 (not_2_out, j_k_ff_2_q);
  not not_3 (not_3_out, j_k_ff_3_q);
  J_K_Flip_Flop j_k_ff_1 (
    .J(in_1), .clk(CLK_out), .K(in_1), .Q(j_k_ff_1_q), .preset(PRESET), .reset(CLEAR));  // open: Qn, en
  J_K_Flip_Flop j_k_ff_2 (
    .J(in_1), .clk(not_1_out), .K(in_1), .Q(j_k_ff_2_q), .preset(PRESET), .reset(CLEAR));  // open: Qn, en
  J_K_Flip_Flop j_k_ff_3 (
    .J(in_1), .clk(not_2_out), .K(in_1), .Q(j_k_ff_3_q), .preset(PRESET), .reset(CLEAR));  // open: Qn, en
  J_K_Flip_Flop j_k_ff_4 (
    .J(in_1), .clk(not_3_out), .K(in_1), .Q(j_k_ff_4_q), .preset(PRESET), .reset(CLEAR));  // open: Qn, en
  not not_4 (not_4_out, j_k_ff_3_q);
  not not_5 (not_5_out, j_k_ff_1_q);
  not not_6 (not_6_out, j_k_ff_2_q);
  not not_7 (not_7_out, j_k_ff_1_q);
  not not_8 (not_8_out, j_k_ff_2_q);
  not not_9 (not_9_out, j_k_ff_3_q);
  not not_10 (not_10_out, j_k_ff_1_q);
  not not_11 (not_11_out, j_k_ff_3_q);
  not not_12 (not_12_out, j_k_ff_1_q);
  not not_13 (not_13_out, j_k_ff_2_q);
  not not_14 (not_14_out, j_k_ff_3_q);
  not not_15 (not_15_out, j_k_ff_1_q);
  not not_16 (not_16_out, j_k_ff_1_q);
  not not_17 (not_17_out, j_k_ff_2_q);
  not not_18 (not_18_out, j_k_ff_1_q);
  not not_19 (not_19_out, j_k_ff_2_q);
  not not_20 (not_20_out, j_k_ff_1_q);
  not not_21 (not_21_out, j_k_ff_3_q);
  not not_22 (not_22_out, j_k_ff_2_q);
  not not_23 (not_23_out, j_k_ff_1_q);
  and and_1 (and_1_out, not_4_out, not_5_out);
  and and_2 (and_2_out, j_k_ff_3_q, j_k_ff_1_q);
  not not_24 (not_24_out, j_k_ff_3_q);
  and and_3 (and_3_out, not_6_out, not_7_out);
  and and_4 (and_4_out, j_k_ff_2_q, j_k_ff_1_q);
  or or_1 (or_1_out, not_8_out, j_k_ff_1_q, j_k_ff_3_q);
  and and_5 (and_5_out, not_9_out, not_10_out);
  and and_6 (and_6_out, not_11_out, j_k_ff_2_q);
  and and_7 (and_7_out, j_k_ff_2_q, not_12_out);
  and and_8 (and_8_out, j_k_ff_3_q, not_13_out, j_k_ff_1_q);
  and and_9 (and_9_out, not_14_out, not_15_out);
  and and_10 (and_10_out, j_k_ff_2_q, not_16_out);
  and and_11 (and_11_out, not_17_out, not_18_out);
  and and_12 (and_12_out, j_k_ff_3_q, not_19_out);
  and and_13 (and_13_out, j_k_ff_3_q, not_20_out);
  and and_14 (and_14_out, not_21_out, j_k_ff_2_q);
  and and_15 (and_15_out, j_k_ff_3_q, not_22_out);
  and and_16 (and_16_out, j_k_ff_3_q, not_23_out);
  or or_2 (or_2_out, and_1_out, j_k_ff_2_q, and_2_out, j_k_ff_4_q);
  or or_3 (or_3_out, not_24_out, and_3_out, and_4_out);
  or or_4 (or_4_out, and_5_out, and_6_out, and_7_out, and_8_out, j_k_ff_4_q);
  or or_5 (or_5_out, and_9_out, and_10_out);
  or or_6 (or_6_out, and_11_out, and_12_out, and_13_out, j_k_ff_4_q);
  or or_7 (or_7_out, and_14_out, and_15_out, and_16_out, j_k_ff_4_q);
  _7_Segment_Display u_7_segment_display_1 (
    .g(or_7_out), .f(or_6_out), .a(or_2_out), .b(or_3_out), .e(or_5_out), .d(or_4_out), .c(or_1_out));  // open: dp
endmodule
