// Logisim project ejercicio 2 5 de febrero.circ as structural Verilog: 1 circuit, main circuit main
module main (
  input  [3:0] in_1,
  input  [3:0] in_2
);

  _7_Segment_Display u_7_segment_display_1 (
    .g(in_1[3]), .f(in_1[2]), .a(in_1[1]), .b(in_1[0]), .e(in_2[0]), .d(in_2[1]), .c(in_2[2]), .dp(in_2[3]));
endmodule
