// Logisim project ejercicio 26 de marzo.circ as structural Verilog: 1 circuit, main circuit main
module main (
  input  [1:0] in_1,
  input  Cin,
  input  [1:0] in_3,
  input  [2:0] in_4,
  output Suma,
  output Cout,
  output out_7
);

  wire and_1_out, and_2_out, and_3_out, and_4_out, or_1_out, xor_1_out, xor_2_out;

  xor xor_1 (xor_1_out, in_1[0], in_1[1]);
  and and_1 (and_1_out, in_1[0], in_1[0], in_1[1]);
  xor xor_2 (xor_2_out, in_3[0], in_3[1]);
  and and_2 (and_2_out, in_3[0], in_3[0], in_3[1]);
  and and_3 (and_3_out, xor_1_out, Cin);
  xor xor_3 (in_4[1], xor_2_out, or_1_out);
  and and_4 (and_4_out, xor_2_out, or_1_out);
  xor xor_4 (in_4[0], xor_1_out, Cin);
  or or_1 (or_1_out, and_3_out, and_1_out);
  or or_2 (in_4[2], and_4_out, and_2_out);

  assign Cout = in_4[2];
  assign out_7 = in_4[1];
  assign Suma = in_4[0];
endmodule
