// Logisim project ejercicio 5 de febrero.circ as structural Verilog: 1 circuit, main circuit main
module main (
  input  A,
  input  B,
  output out_3,
  output out_4
);

  wire and_1_out, not_1_out, not_2_out;

  not not_1 (not_1_out, A);
  not not_2 (not_2_out, B);
  and and_1 (and_1_out, A, B);
  not not_3 (out_3, and_1_out);
  or or_1 (out_4, not_1_out, not_2_out, not_2_out);
endmodule
